# Fritzing sketch speaker-sketch (saved by Fritzing 0.9.2b)
breadboards: 1

parts:
  Arduino_Pro_Mini_3_3V_8_MHz = Arduino Pro Mini v13
  8_Ohm_1_W_speaker = SPEAKER [package=pcb_mount_speaker]
  NPN_transistor = TRANSISTOR_NPN [package=to-92]
  R1 = Resistor [tolerance=±5% resistance=22 package="2010 [SMD]"]

nets:
  N1: Arduino_Pro_Mini_3_3V_8_MHz.GND, 8_Ohm_1_W_speaker.-
  N2: Arduino_Pro_Mini_3_3V_8_MHz.VCC, NPN_transistor.C
  N3: Arduino_Pro_Mini_3_3V_8_MHz.D9_PWM, R1.Pin_0
  N4: 8_Ohm_1_W_speaker.+, NPN_transistor.E
  N5: NPN_transistor.B, R1.Pin_1
